# Fritzing sketch FS_2S_OpAm (saved by Fritzing 0.9.3b)
circuit board: 4.63688cm x 3.59792cm

parts:
  FlexS1 = Basic Flex Resistor
  R1 = Resistor [tolerance=±5% resistance=10k package="0603 [SMD]"]
  FlexS2 = Basic Flex Resistor
  R1_2 = Resistor [tolerance=±5% resistance=10k package="0603 [SMD]"]
  V1 = DC Power [voltage=5]
  LM358 = LM358 [package=dip08]

nets:
  N1: FlexS1.Pin_2, FlexS2.Pin_2, V1.V+, LM358.G$1_V+
  N2: FlexS1.pin_1, R1.Pin_0, LM358.G$1_+IN
  GND: R1.Pin_1, R1_2.Pin_1, V1.V-, LM358.G$1_V-
  N3: FlexS2.pin_1, R1_2.Pin_0, LM358.G$2_+IN
  N4: LM358.G$1_OUT, LM358.G$1_-IN
  N5: LM358.G$2_-IN, LM358.G$2_OUT
