# Fritzing sketch FlexSensorSketch (saved by Fritzing 0.9.3b)
circuit board: 3.3cm x 3.3cm
breadboards: 1

parts:
  Lily = LilyPad Arduino Simple Board
  R7 = Resistor [tolerance=±5% resistance=47k package=THT]
  R8 = Basic Flex Resistor
  R5 = Resistor [tolerance=±5% resistance=47k package=THT]
  R3 = Resistor [tolerance=±5% resistance=47k package=THT]
  R1 = Resistor [tolerance=±5% resistance=47k package=THT]
  R6 = Basic Flex Resistor
  R4 = Basic Flex Resistor
  R2 = Basic Flex Resistor

nets:
  N1: Lily.A2, R1.Pin_1, R2.pin_1
  N2: Lily.A3, R3.Pin_1, R4.pin_1
  N3: Lily.A4, R5.Pin_1, R6.pin_1
  N4: Lily.A5, R7.Pin_1, R8.pin_1
  N5: Lily.GND, R7.Pin_0, R5.Pin_0, R3.Pin_0, R1.Pin_0
  N6: Lily.VCC, R8.Pin_2, R6.Pin_2, R4.Pin_2, R2.Pin_2
