# Fritzing sketch FlexSensorSketch5S (saved by Fritzing 0.9.3b)
circuit board: 3cm x 4.2cm
breadboards: 1

parts:
  R9 = Resistor [tolerance=±5% resistance=47k package=THT]
  R10 = Basic Flex Resistor
  R7 = Resistor [tolerance=±5% resistance=47k package=THT]
  R5 = Resistor [tolerance=±5% resistance=47k package=THT]
  R3 = Resistor [tolerance=±5% resistance=47k package=THT]
  R8 = Basic Flex Resistor
  R6 = Basic Flex Resistor
  R4 = Basic Flex Resistor
  R2 = Basic Flex Resistor
  R1 = Resistor [tolerance=±5% resistance=47k package=THT]

nets:
  N1: R9.Pin_0, R7.Pin_0, R5.Pin_0, R3.Pin_0, R1.Pin_0
  N2: R9.Pin_1, R10.pin_1
  N3: R10.Pin_2, R8.Pin_2, R6.Pin_2, R4.Pin_2, R2.Pin_2
  N4: R7.Pin_1, R8.pin_1
  N5: R5.Pin_1, R6.pin_1
  N6: R3.Pin_1, R4.pin_1
  N7: R2.pin_1, R1.Pin_1
